# Fritzing sketch AmbulanceSiren (saved by Fritzing 0.9.3b)
breadboards: 1

parts:
  Часть1 = Arduino Uno (Rev3)
  LED1 = LED - 5mm [color="Red (633nm)" package="5 mm [THT]"]
  LED2 = LED - 5mm [color="Red (633nm)" package="5 mm [THT]"]
  LED3 = LED - 5mm [color="Blue (430nm)" package="5 mm [THT]"]
  LED4 = LED - 5mm [color="Blue (430nm)" package="5 mm [THT]"]
  R1 = Resistor [tolerance=±5% resistance=220 package=THT]
  R2 = Resistor [tolerance=±5% resistance=220 package=THT]
  R3 = Resistor [tolerance=±5% resistance=220 package=THT]
  R4 = Resistor [tolerance=±5% resistance=220 package=THT]
  J1 = Piezo Speaker

nets:
  N1: Часть1.D8, J1.pin2
  N2: Часть1.D2, R4.Pin_1
  N3: Часть1.D3_PWM, R3.Pin_1
  N4: Часть1.D4, R2.Pin_1
  N5: Часть1.D5_PWM, R1.Pin_1
  N6: Часть1.GND, LED1.cathode, LED2.cathode, LED3.cathode, LED4.cathode, J1.pin1
  N7: LED1.anode, R1.Pin_0
  N8: LED2.anode, R2.Pin_0
  N9: LED3.anode, R3.Pin_0
  N10: LED4.anode, R4.Pin_0

// code stored in the sketch: AmbulanceSiren.ino
#include "pitches.h"

// bvik
// Ambulance siren 

// notes in the melody:
int melody[] = {NOTE_C5, NOTE_F5};
int duration = 800;  
int minPin = 2;
int maxPin = 5;
 
void setup() {
	for (int i = minPin; i <= maxPin; i++) {
	  pinMode(i,OUTPUT);
	}
}
 
void loop() {  
  for (int thisNote = 0; thisNote < 2; thisNote++) {
		for (int i = minPin; i <= maxPin; i++) {
	  	digitalWrite(i, LOW);
		}

    tone(8, melody[thisNote], duration);

    digitalWrite(minPin + thisNote*2, HIGH);
    digitalWrite(minPin + thisNote*2 + 1, HIGH);

    delay(duration);
  }
}
