# Fritzing sketch ImperialMarch (saved by Fritzing 0.9.3b)
breadboards: 1

parts:
  J1 = Piezo Speaker
  LED1 = LED - 5mm [color="White (4500K)" package="5 mm [THT]"]
  LED2 = LED - 5mm [color="Yellow (595nm)" package="5 mm [THT]"]
  LED3 = LED - 5mm [color="Blue (430nm)" package="5 mm [THT]"]
  LED4 = LED - 5mm [color="Red (633nm)" package="5 mm [THT]"]
  LED5 = LED - 5mm [color="Green (570nm)" package="5 mm [THT]"]
  R1 = Resistor [tolerance=±5% resistance=220 package=THT]
  R2 = Resistor [tolerance=±5% resistance=220 package=THT]
  R3 = Resistor [tolerance=±5% resistance=220 package=THT]
  R4 = Resistor [tolerance=±5% resistance=220 package=THT]
  R5 = Resistor [tolerance=±5% resistance=220 package=THT]
  Часть1 = Arduino Uno (Rev3)

nets:
  N1: J1.pin1, LED1.cathode, LED2.cathode, LED3.cathode, LED4.cathode, LED5.cathode, Часть1.GND
  N2: J1.pin2, Часть1.D8
  N3: LED1.anode, R1.Pin_1
  N4: LED2.anode, R2.Pin_1
  N5: LED3.anode, R3.Pin_1
  N6: LED4.anode, R4.Pin_1
  N7: LED5.anode, R5.Pin_1
  N8: R1.Pin_0, Часть1.D7
  N9: R2.Pin_0, Часть1.D6_PWM
  N10: R3.Pin_0, Часть1.D5_PWM
  N11: R4.Pin_0, Часть1.D4
  N12: R5.Pin_0, Часть1.D2

// code stored in the sketch: ImperialMarch.ino
const byte COUNT = 39;
const double MULT = 1.5;
const byte LED_MIN = 2; 
const byte LED_MAX = 8;
int PIN_BUZZER = 8;


int frequences[COUNT] = {
  392, 392, 392, 311, 466, 392, 311, 466, 392,
  587, 587, 587, 622, 466, 369, 311, 466, 392,
  784, 392, 392, 784, 739, 698, 659, 622, 659,
  415, 554, 523, 493, 466, 440, 466,
  311, 369, 311, 466, 392
};
int durations[COUNT] = {
  350, 350, 350, 250, 100, 350, 250, 100, 700,
  350, 350, 350, 250, 100, 350, 250, 100, 700,
  350, 250, 100, 350, 250, 100, 100, 100, 450,
  150, 350, 250, 100, 100, 100, 450,
  150, 350, 250, 100, 750
};


void setup() {
  
  for (int i = LED_MIN; i <= LED_MAX; i++ ) {
     if (i != 3)
       pinMode(i, OUTPUT);  
  }
}

void loop() {
  for (int i = 0; i < COUNT; i++) {
    tone(PIN_BUZZER, frequences[i], durations[i]*MULT);
    for (int i = LED_MIN; i <= LED_MAX; i++ ) {
       if (i != 3)
        analogWrite(i, random(0, 254));  
    }    
    delay(durations[i]*MULT);  
  }
  noTone(PIN_BUZZER);
  for (int i = LED_MIN; i <= LED_MAX; i++ ) {
       if (i != 3)
         analogWrite(i, 0);  
    }    
  delay(500);
}
